# Fritzing sketch Conveyor Circuit (saved by Fritzing 0.9.2b)

parts:
  Part1 = Arduino Uno (Rev3) - ICSP
  U1 = ESP8266 NodeMCU LoLin module
  L298N1 = L298N DC motor driver
  S1 = Round Pushbutton
  Part2 = LCD1602-I2C
  Part3 = SRF05 Ultrasonic Rangefinder
  J2 = Basic Servo
  R1 = Resistor [tolerance=±5% resistance=220 package="1206 [SMD]"]  # not connected
  M1 = DC Motor
  J3 = Basic Servo
  J1 = Infrared Proximity Sensor

nets:
  GND: Part1.GND, U1.GND, L298N1.GND, Part3.GND
  3V3: Part1.3V3, U1.3V3
  5V: Part1.5V, J3.vcc
  VIN: Part1.VIN, L298N1.12V
  N1: U1.D0, J1.Vout
  N2: U1.D1, Part2.SCL
  N3: U1.D2, Part2.SDA
  N4: U1.D3, Part3.Echo
  N5: U1.D4, S1.leg0
  N6: U1.D5, J2.pulse
  N7: U1.D6, J3.pulse
  N8: U1.D7, Part3.Trig
  N9: U1.D8, L298N1.IN4
  N10: L298N1.OUT3, M1.pin_2
  N11: L298N1.OUT4, M1.pin_1

custom parts:
  ESP8266 NodeMCU LoLin module: ESP8266 based NodeMCU
  L298N DC motor driver: 2x DC motor driver with 78M05 positive voltage regulator (7..35 V) L298N: max 46 V, 2 A Set 5 V Enable jumper to enable 5 V regultor (needed for the L298N) and +5 V output at screw terminal or supply external +5 V at screw terminal Set ENA and/or ENB to +5 V to enable motor permanently or supply ENA and/or ENB with PWM signal IN1 and IN2 set rotation directory for motor A (OUT1/OUT2) IN2 and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
  LCD1602-I2C: A standard character display, usually with 2x16 characters. Comes in many colors with LCM1602 IIC attached.
